# Fritzing sketch T_H_S (saved by Fritzing 0.9.0b)
breadboards: 1

parts:
  U1 = atmega328 [package=dip]
  Part1 = FTDI Basic Programmer
  XTAL1 = Crystal [frequency="16 Mhz" package=THT]
  C3 = Ceramic Capacitor [capacitance=22µF package="0603 [SMD, multilayer]"]
  C4 = Ceramic Capacitor [capacitance=0.1µF package="0603 [SMD, multilayer]"]
  C2 = Ceramic Capacitor [capacitance=22µF package="0603 [SMD, multilayer]"]
  R1 = Resistor [tolerance=±20% resistance=1k package=THT]
  J1 = Piezo Speaker [part_number="Piezo speaker"]
  J2 = Piezo Speaker [part_number="vibration sensor"]
  T1 = LM35 Temperature Sensor [package="TO92 [THT]"]
  LED1 = LED - 5mm [color="Red (633nm)" package="5 mm [THT]"]
  R2 = Resistor [tolerance=±5% resistance=220 package=THT]
  BAT1 = Battery Holders [package=battery-aa-kit]
  Part2 = PowerBoost 1000 Basic
  LCD_I2C1 = LCD screen I2C  # not connected
  S1 = Toggle Switch [package=THT]
  S2 = Round Pushbutton
  S3 = Round Pushbutton
  S4 = Toggle Switch [package=THT]
  D1 = Diode [package=diode-1n4001]
  D2 = Diode [package=diode-1n4001]  # not connected
  D3 = Diode [package=diode-1n4001]  # not connected
  D4 = Diode [package=diode-1n4001]

nets:
  N1: U1.RESET, C4.1, R1.Pin_0
  N2: U1.D0_(RX), Part1.TXO
  N3: U1.D1_(TX), Part1.RXI
  N4: U1.VCC, U1.D9_(PWM), U1.AVCC, R1.Pin_1, J1.pin1, J1.pin2, T1.+Vs
  GND: U1.GND, Part1.GND, C3.1, C2.0, J2.pin1, T1.GND, R2.Pin_0, BAT1.+, Part2.GND, S2.leg1, S3.leg1
  N5: U1.XLAT1, XTAL1.pin_1, C3.0
  N6: U1.XLAT2, XTAL1.pin_0, C2.1
  N7: U1.D5_(PWM), S2.leg0
  N8: U1.D6_(PWM), S3.leg0
  N9: U1.D10_(PWM), LED1.anode
  N10: U1.A0, J2.pin2
  N11: U1.A1, T1.Vout
  N12: Part1.DTR, C4.0
  N13: Part1.POWER, Part2.5.0V, S1.L2
  N14: LED1.cathode, R2.Pin_1
  N15: BAT1.-, S4.COM
  N16: Part2.VBAT, S4.L2
  N17: S1.COM, D1.A, D4.A

custom parts:
  PowerBoost 1000 Basic: The PowerBoost 1000 is a little DC/DC boost converter module that can run from 1.8V batteries or higher, and convert the battery output to 5.2V DC for running your 5V projects. At its heart is a TPS61030 boost converter from TI. This boost converter chip has some really nice extras such as low battery detection, 4A internal switch, synchronous conversion, excellent efficiency, and 700KHz high-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
  LCD screen I2C: Character display, I2C interface, 2x16 characters.
